# Fritzing sketch devpola-gpio-schematic (saved by Fritzing 0.9.3b)
breadboards: 1
stripboards: 1

parts:
  Part1 = Thermal Printer
  U1 = LIPO-2000mAh [package=lipo-2000]
  U2 = LIPO-2000mAh [package=lipo-2000]
  U3 = TRANSCHIPTC5747 [package=camera_sfv24r-2st_2]  # not connected
  S1 = Round Pushbutton [part_number=Shutter]
  S2 = Round Pushbutton
  LED1 = LED - 3mm [color="Red (633nm)" package="3 mm [THT]"]
  R1 = Resistor [tolerance=±5% resistance=220 package="2010 [SMD]"]
  IC1 = IC, DIP package, 4 pins [part_number="DC DC Converter" chip_label=IC]  # not connected
  S3 = Toggle Switch [package=THT]
  Raspberry_Pi1 = Raspberry Pi 3 [part_number=RPI-3-V1.2]

nets:
  N1: Part1.GND#0, U1.-, U2.-
  N2: Part1.VH, S3.COM
  N3: Part1.GND#2, S1.leg0, S2.leg0, LED1.cathode, LED1.anode, R1.Pin_0, R1.Pin_1, Raspberry_Pi1.GND
  N4: Part1.RXD, Raspberry_Pi1.GIPO14
  N5: U1.+, U2.+, S3.L2
  N6: S1.leg1, Raspberry_Pi1.GIPO27
  N7: S2.leg1, Raspberry_Pi1.GIPO17

notes:
  7.4V
  5V
  Display
  shutter
  info
  symbolic for 7.4V LIPO battery
  symbolic for DC-DC converter
  symbolic for on-off switch
